// Logisim project Prvi projekat - LogiSim.circ as structural Verilog
module Prvo_logicko_kolo (
  input  X1,
  input  X2,
  output Y
);

  wire not_1_out, or_1_out;

  not not_1 (not_1_out, X1);
  // Probe on or_1_out
  or or_1 (or_1_out, X2, X1);
  and and_1 (Y, or_1_out, not_1_out);
  // Probe on Y
endmodule
